# Fritzing sketch Web_home_automation_ckt_diagram (saved by Fritzing 0.8.7b)
breadboards: 2

parts:
  Raspberry_Pi_1 = Raspberry Pi 4 [part_number=RPI-4-b]
  U1 = atmega328 [package=dip]
  Mod1 = Raspberry Pi Pico
  Q1 = MOSFET-NCHANNEL [package=to220v]
  R1 = Resistor [tolerance=±5% resistance=10k package=THT]
  K1 = Relay [part_number=FRS1B-S package=THT]
  D1 = Diode [package=diode-1n4001]
  JP1 = Header 2 [package=springterminal-2.54mm-2]
  R2 = Photocell (LDR) [package=THT]
  R3 = Resistor [tolerance=±5% resistance=10k package=THT]
  DHT1 = DHT11 Humitidy and Temperature Sensor
  IC1 = LM324 [package=dil16]
  R4 = Resistor [tolerance=±5% resistance=10k package=THT]
  R5 = Resistor [tolerance=±5% resistance=10k package=THT]
  U2 = SWITCH_SPDT [package=kps-1290]
  S1 = Pushbutton [package="[THT]"]
  S2 = Pushbutton [package="[THT]"]
  S3 = Pushbutton [package="[THT]"]
  S4 = Pushbutton [package="[THT]"]
  D2 = Schottky Diode [part_number=1N5817 package="300 mil [THT]"]
  U3 = LCD-16X2 [package=lcd-16x2]
  R6 = Resistor [tolerance=±5% resistance=220 package=THT]
  R7 = Rotary Potentiometer (Large) [maximum_resistance=100kΩ package=THT]

nets:
  N1: Raspberry_Pi_1.3v3, Raspberry_Pi_1.GPIO17, Raspberry_Pi_1.GPIO22, Raspberry_Pi_1.GPIO23, Mod1.pin_39, U2.P, S1.Pin_1, S1.Pin_2, S2.Pin_3, S2.Pin_4, S3.Pin_3, S3.Pin_4, S4.Pin_3, S4.Pin_4
  N2: Raspberry_Pi_1.GPIO27, S1.Pin_3, S1.Pin_4
  N3: Raspberry_Pi_1.GPIO10, IC1.IN1+
  N4: Raspberry_Pi_1.GPIO24, IC1.IN4+
  N5: Raspberry_Pi_1.GPIO18, U2.O
  N6: Raspberry_Pi_1.GPIO15, Mod1.pin_1
  N7: Raspberry_Pi_1.GPIO14, Mod1.pin_2
  GND: Raspberry_Pi_1.GND, Mod1.pin_3, Mod1.pin_8, Mod1.pin_13, Mod1.pin_18, Mod1.pin_23, Mod1.pin_28, Mod1.pin_33, Mod1.pin_38, Mod1.pin_42, Q1.S, R1.Pin_0, R3.Pin_1, DHT1.GND, IC1.IN1-, IC1.IN2-, IC1.IN3-, IC1.IN3+, IC1.GND, IC1.IN4-, R5.Pin_1, U3.VSS, U3.R_W, U3.K, R7.leg1
  VDD: Raspberry_Pi_1.5V, U1.VCC, K1.COIL1, D1.A, DHT1.VDD, IC1.V+, R4.Pin_1, U3.VDD, R6.Pin_0, R7.leg2
  N8: U1.RESET, R4.Pin_0
  N9: U1.D0_(RX), Mod1.pin_6, R5.Pin_0
  N10: U1.D2, U3.DB7
  N11: U1.D3_(PWM), U3.DB6
  N12: U1.D4, U3.DB5
  N13: U1.D5_(PWM), U3.DB4
  N14: U1.D7, DHT1.DATA
  N15: U1.D11_(PWM), U3.E
  N16: U1.D12, U3.RS
  N17: Mod1.pin_4, Q1.G, R1.Pin_1, D2.cathode
  N18: Mod1.pin_5, IC1.IN2+
  N19: Mod1.pin_34, R2.pin_1, R3.Pin_0
  N20: Mod1.pin_35, Mod1.pin_36, R2.pin_0
  N21: Q1.D, K1.COIL2
  N22: K1.C1, K1.C2, JP1.2
  N23: IC1.OUT1, D2.anode
  N24: S2.Pin_1, S2.Pin_2
  N25: S3.Pin_1, S3.Pin_2
  N26: S4.Pin_1, S4.Pin_2
  N27: U3.VO, R7.wiper
  N28: U3.A, R6.Pin_1

notes:
  Short pin 3.3Vout and A_VREF pin of raspberry pi pico to remove reading fluctuations.
  The power requirement of the circuit is somehow more than the raspberry pi can supply I suggest using a transformer with a rectifier and with a buck converter to power the curcuits.
  Add a 16Mhz crystal oscillator at the xtal pins of ATmega328. This one is optional.
  connect these three outputs with a triac or a relay. use diodes to prevent reverse polarity.

custom parts:
  Raspberry Pi 4: The RPi4, a faster version of the awesome Raspberry Pi 2 B ARM Board with 40 pin gpio. Ready for special Raspberry Pi B+ and RPi2 Hat (Hardware attached (on) top)
  Raspberry Pi Pico: Raspberry Pi Pico. Based around the RP2040 microcontroller the Pico is a low cost microcontroller device bringing Raspberry Pi quality, cost, and easy of use to the microcontroller space. Jan 2021, Split part in to two versions: tht (this one) and SMD. This one will drill holes for a .1 in header in pcb to allow plugging in the module as well as providing pads to solder the module to the top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
  DHT11 Humitidy and Temperature Sensor: DHT11 Humidity and Temperature Sensor
  LM324: LM324 Quad OpAmp
